# Fritzing sketch Joystick Fritzet (saved by Fritzing 0.9.3b)
breadboards: 2

parts:
  Part1 = Black Joystick KY-023
  M1 = DOIT Esp32 DevKit v1 (30 pins long, 11 pins width) [part_number=ESP32S-PIN30]
  LCD1 = LCD screen
  LCM1602_IIC1 = LCM1602 IIC [part_number="LCM1602 IIC" chip_label="LCM1602 IIC" package="DIP (Dual Inline) [THT]"]

nets:
  N1: Part1.SW, M1.D15
  N2: Part1.VRy, M1.D34
  N3: Part1.VRx, M1.D35
  +5V: Part1.+5V, M1.3V3, LCM1602_IIC1.VCC
  GND: Part1.GND, M1.GND, LCM1602_IIC1.GND
  N4: M1.D21, LCM1602_IIC1.SDA
  N5: M1.D22, LCM1602_IIC1.SCL
  VSS: LCD1.VSS, LCM1602_IIC1.VSS
  VDD: LCD1.VDD, LCM1602_IIC1.VDD
  N6: LCD1.V0, LCM1602_IIC1.V0
  N7: LCD1.RS, LCM1602_IIC1.RS
  N8: LCD1.R/W, LCM1602_IIC1.RW
  N9: LCD1.E, LCM1602_IIC1.E
  N10: LCD1.DB0, LCM1602_IIC1.D0
  N11: LCD1.DB1, LCM1602_IIC1.D1
  N12: LCD1.DB2, LCM1602_IIC1.D2
  N13: LCD1.DB3, LCM1602_IIC1.D3
  N14: LCD1.DB4, LCM1602_IIC1.D4
  N15: LCD1.DB5, LCM1602_IIC1.D5
  N16: LCD1.DB6, LCM1602_IIC1.D6
  N17: LCD1.DB7, LCM1602_IIC1.D7
  N18: LCD1.LED+, LCM1602_IIC1.A
  N19: LCD1.LED-, LCM1602_IIC1.K
  N20: LCM1602_IIC1.LED_A, LCM1602_IIC1.LED_B

custom parts:
  Black Joystick KY-023: Description: The joystick is a combination of 2 analoog potentiometer and a digital switch. Arduino GND --> Module pin - Arduino +5V --> Module pin +5V Arduino Analoog 0 --> Module VRx Arduino Analoog 1 --> Module VRy Arduino Digital --> Module SW Dimensions: 1" x 1.25"
  DOIT Esp32 DevKit v1 (30 pins long, 11 pins width): The DOIT Esp32 DevKit v1 is one of the development board created by DOIT to evaluate the ESP-WROOM-32 module. It is based on the ESP32 microcontroller that boasts Wifi, Bluetooth, Ethernet and Low Power support all in a single chip. (vanepp) made breadboard work, adjusted pin numbering and labels and reduced size of schematic and cleaned up pcb. This chip is 30pins long (2 x15) and 11 pins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
  LCM1602 IIC: I2C-Module to use a 1602 or 2004 LCD on with the wire.h libory Serial LCD Modul
